# Fritzing sketch vending Machine Diagram (saved by Fritzing 0.9.3b)
breadboards: 1

parts:
  Part1 = Arduino Mega 2560 (Rev3)
  Part2 = 16-Channel 12-bit PWM Servo Driver - I2C [part_number=815]
  J1 = Basic Servo
  J2 = Basic Servo
  J3 = Basic Servo
  J4 = Basic Servo
  Keypad4x1 = Keypad Membran 4x4
  JACK1 = 2.1mm Barrel Jack with Terminal Block
  Part7 = HX711 Weighing Sensor Module
  Load_Cell3 = Load Cell - Red/white/black/green
  LED3 = LEDs [package=led10mm]
  LED4 = LEDs [package=led10mm]
  LED5 = LEDs [package=led10mm]
  IR1 = TSOP312.., 314.. [package=THT]
  IR2 = TSOP312.., 314.. [package=THT]
  IR3 = TSOP312.., 314.. [package=THT]
  SERVO1 = Tower Pro SG90 servo [part_number=101246]
  SERVO2 = Tower Pro SG90 servo [part_number=101246]
  SERVO3 = Tower Pro SG90 servo [part_number=101246]
  J5 = Basic Servo
  LCM1602_IIC3 = LCM1602 IIC [part_number="LCM1602 IIC" chip_label="LCM1602 IIC" package="DIP (Dual Inline) [THT]"]
  LCD1 = LCD screen

nets:
  N1: Part1.A0, IR1.Data
  N2: Part1.A1, IR2.Data
  N3: Part1.A2, IR3.Data
  N4: Part1.D21/SCL, Part1.SCL, Part2.SCL, LCM1602_IIC3.SCL
  N5: Part1.D20/SDA, Part1.SDA, Part2.SDA, LCM1602_IIC3.SDA
  N6: Part1.D11_PWM, Part7.CK/TX
  N7: Part1.D10_PWM, Part7.DO/RX
  N8: Part1.D9_PWM, Keypad4x1.Pin1
  N9: Part1.D8_PWM, Keypad4x1.Pin2
  N10: Part1.3V3, LED3.A, LED4.A, LED5.A
  VCC: Part1.5V, Part2.VCC, Part7.VCC, LCM1602_IIC3.VCC
  GND: Part1.GND, Part2.GND, J1.gnd, J2.gnd, J3.gnd, J4.gnd, JACK1.NEG, Part7.GND, LED3.C, LED4.C, LED5.C, SERVO1.GND, SERVO2.GND, SERVO3.GND, LCM1602_IIC3.GND
  N11: Part1.D2_PWM, Keypad4x1.Pin8
  N12: Part1.D3_PWM, Keypad4x1.Pin7
  N13: Part1.D4_PWM, Keypad4x1.Pin6
  N14: Part1.D5_PWM, Keypad4x1.Pin5
  N15: Part1.D6_PWM, Keypad4x1.Pin4
  N16: Part1.D7_PWM, Keypad4x1.Pin3
  N17: Part2.PWRIN, JACK1.POS
  N18: Part2.PWM7, SERVO1.Signal
  VCC_2: Part2.5.0V, J1.vcc, J2.vcc, J3.vcc, J4.vcc, SERVO1.+5V, SERVO2.+5V, SERVO3.+5V, J5.vcc
  N19: Part2.PWM6, SERVO3.Signal
  N20: Part2.PWM5, SERVO2.Signal
  N21: Part2.PWM4, J5.pulse
  N22: Part2.PWM3, J2.pulse
  N23: Part2.PWM2, J3.pulse
  N24: Part2.PWM0, J1.pulse, J4.pulse
  N25: Part7.E+, Load_Cell3.wire1
  N26: Part7.E-, Load_Cell3.wire3
  N27: Part7.A+, Load_Cell3.wire2
  N28: Part7.A-, Load_Cell3.wire4
  VSS: LCM1602_IIC3.VSS, LCD1.VSS
  VDD: LCM1602_IIC3.VDD, LCD1.VDD
  N29: LCM1602_IIC3.V0, LCD1.V0
  N30: LCM1602_IIC3.RS, LCD1.RS
  N31: LCM1602_IIC3.RW, LCD1.R/W
  N32: LCM1602_IIC3.E, LCD1.E
  N33: LCM1602_IIC3.D0, LCD1.DB0
  N34: LCM1602_IIC3.D1, LCD1.DB1
  N35: LCM1602_IIC3.D2, LCD1.DB2
  N36: LCM1602_IIC3.D3, LCD1.DB3
  N37: LCM1602_IIC3.D4, LCD1.DB4
  N38: LCM1602_IIC3.D5, LCD1.DB5
  N39: LCM1602_IIC3.D6, LCD1.DB6
  N40: LCM1602_IIC3.D7, LCD1.DB7
  N41: LCM1602_IIC3.A, LCD1.LED+
  N42: LCM1602_IIC3.K, LCD1.LED-

custom parts:
  16-Channel 12-bit PWM Servo Driver - I2C: You want to make a cool robot, maybe a hexapod walker, or maybe just a piece of art with a lot of moving parts. Or maybe you want to drive a lot of LEDs with precise PWM output. Using only two pins, control 16 free-running PWM outputs! You can even chain up 62 breakouts to control up to 992 PWM outputs.
  Keypad Membran 4x4: Membrane Keypad 4x4 Matrix
  HX711 Weighing Sensor Module: HX711 is a precision 24-bit analog-to-digital converter (ADC) designed for weigh scales and industrial control applications to interface directly with a bridge sensor.
  Load Cell - Red/white/black/green: A rectangle load cell/weighting pressure Sensor with four wires - Red, white, black, green. Normally corresponding with E+, E-, A+, A- respectively.
  Tower Pro SG90 servo: Original file by John De Cristofaro http://www.adafruit.com/products/1449 Adafruit Feedback Servo (Small) Edited by: e-radionica.com 28/9/2015
  LCM1602 IIC: I2C-Module to use a 1602 or 2004 LCD on with the wire.h libory Serial LCD Modul
